// Digital circuit frontpanel.dig as structural Verilog
module frontpanel (
  input  clock,
  input  erun,
  input  DC,
  output [15:0] R0,
  output [15:0] R1,
  output [15:0] R2,
  output [15:0] R3,
  output [7:0] PC,
  output halt,
  output error
);

  wire dipswitch_1_out, hex, hexdisplay_1_p2, hexdisplay_1_p5, hexdisplay_1_p8, hexdisplay_1_p10,
       hexdisplay_1_p13, hexdisplay_2_p4, hexdisplay_2_p7, hexdisplay_2_p10, hexdisplay_2_p12,
       hexdisplay_2_p15, instrdisplay_1_p1, instrdisplay_1_p2, instrdisplay_1_p3, instrdisplay_1_p4,
       instrdisplay_1_p5, instrdisplay_1_p6, jump, L, or_1_out, R, rd_valid, regdisplay_1_p1,
       regdisplay_1_p2, regdisplay_2_p3, regdisplay_2_p7, rj32_1_p1, rj32_1_p4, rj32_1_p18, rj32_1_p25, rs,
       rs_valid, run_out, step_out;
  wire [1:0] rd;
  wire [2:0] cond;
  wire [3:0] hexdisplay_1_p1, hexdisplay_1_p4, hexdisplay_1_p6, hexdisplay_1_p9, hexdisplay_1_p12,
       hexdisplay_2_p3, hexdisplay_2_p6, hexdisplay_2_p8, hexdisplay_2_p11, hexdisplay_2_p14;
  wire [4:0] op;
  wire [7:0] rj32_1_p2;
  wire [13:0] rj32_1_p6;
  wire [15:0] Data_d, instrdisplay_1_d1, instrdisplay_1_d2, instrdisplay_1_d3, instrdisplay_1_d4,
       instrdisplay_1_d5, instrdisplay_1_d6, Program_d, regdisplay_1_d1, regdisplay_1_d2, regdisplay_2_p1,
       regdisplay_2_p5, rj32_1_p5;

  SixteenSeg sixteenseg_1 (.led(regdisplay_1_d1), .dp(regdisplay_1_p1));
  SixteenSeg sixteenseg_2 (.led(regdisplay_1_d2), .dp(regdisplay_1_p2));
  regdisplay regdisplay_1 (
    .D1(regdisplay_1_d1), .P1(regdisplay_1_p1), .D2(regdisplay_1_d2), .P2(regdisplay_1_p2), .E(1'b1),
    .J(jump), .R(rd));
  BlockRAMDualPort #(.AddrBits(8), .isProgramMemory("true"), .Bits(16)) Program (
    .A(rj32_1_p2), .Din({16{1'b0}}), .str(1'b0), .C(rj32_1_p1), .D(Program_d));
  BlockRAMDualPort #(.AddrBits(14), .Bits(16)) Data (
    .A(rj32_1_p6), .Din(rj32_1_p5), .str(rj32_1_p4), .C(rj32_1_p1), .D(Data_d));
  Button step (.out(step_out));
  Button run (.out(run_out));
  Seven_Seg_Hex seven_seg_hex_1 (.d(hexdisplay_1_p1), .dp(hexdisplay_1_p2));
  Seven_Seg_Hex seven_seg_hex_2 (.d(hexdisplay_1_p4), .dp(hexdisplay_1_p5));
  // hexdisplay hexdisplay_1: pin names not known; wires that end beside it: hexdisplay_1_p1, hexdisplay_1_p2, rd_valid, hexdisplay_1_p4, hexdisplay_1_p5, hexdisplay_1_p6, L, hexdisplay_1_p8, hexdisplay_1_p9, hexdisplay_1_p10, hex, hexdisplay_1_p12, hexdisplay_1_p13
  or or_1 (or_1_out, run_out, erun);
  // rj32 rj32_1: pin names not known; wires that end beside it: rj32_1_p1, rj32_1_p2, Program_d, rj32_1_p4, rj32_1_p5, rj32_1_p6, Data_d, jump, or_1_out, rd_valid, rs_valid, step_out, op, cond, clock, L, R, rj32_1_p18, rd, PC, R0, R1, R2, R3, rj32_1_p25, halt
  Seven_Seg_Hex seven_seg_hex_3 (.d(hexdisplay_1_p6), .dp(hexdisplay_1_p8));
  Seven_Seg_Hex seven_seg_hex_4 (.d(hexdisplay_1_p9), .dp(hexdisplay_1_p10));
  Seven_Seg_Hex seven_seg_hex_5 (.d(hexdisplay_1_p12), .dp(hexdisplay_1_p13));
  SixteenSeg sixteenseg_3 (.led(instrdisplay_1_d1), .dp(instrdisplay_1_p1));
  SixteenSeg sixteenseg_4 (.led(instrdisplay_1_d2), .dp(instrdisplay_1_p2));
  instrdisplay instrdisplay_1 (
    .D1(instrdisplay_1_d1), .P1(instrdisplay_1_p1), .D2(instrdisplay_1_d2), .P2(instrdisplay_1_p2),
    .D3(instrdisplay_1_d3), .P3(instrdisplay_1_p3), .D4(instrdisplay_1_d4), .P4(instrdisplay_1_p4),
    .D5(instrdisplay_1_d5), .P5(instrdisplay_1_p5), .D6(instrdisplay_1_d6), .P6(instrdisplay_1_p6), .I(op),
    .C(cond));
  SixteenSeg sixteenseg_5 (.led(instrdisplay_1_d3), .dp(instrdisplay_1_p3));
  SixteenSeg sixteenseg_6 (.led(instrdisplay_1_d4), .dp(instrdisplay_1_p4));
  SixteenSeg sixteenseg_7 (.led(instrdisplay_1_d5), .dp(instrdisplay_1_p5));
  SixteenSeg sixteenseg_8 (.led(instrdisplay_1_d6), .dp(instrdisplay_1_p6));
  LED stalled (.in(rj32_1_p18));
  Seven_Seg_Hex seven_seg_hex_6 (.d(hexdisplay_2_p3), .dp(hexdisplay_2_p4));
  Seven_Seg_Hex seven_seg_hex_7 (.d(hexdisplay_2_p6), .dp(hexdisplay_2_p7));
  // hexdisplay hexdisplay_2: pin names not known; wires that end beside it: rs, error, hexdisplay_2_p3, hexdisplay_2_p4, 1'b1, hexdisplay_2_p6, hexdisplay_2_p7, hexdisplay_2_p8, R, hexdisplay_2_p10, hexdisplay_2_p11, hexdisplay_2_p12, hex, hexdisplay_2_p14, hexdisplay_2_p15
  LED skip (.in(rj32_1_p25));
  Seven_Seg_Hex seven_seg_hex_8 (.d(hexdisplay_2_p8), .dp(hexdisplay_2_p10));
  Seven_Seg_Hex seven_seg_hex_9 (.d(hexdisplay_2_p11), .dp(hexdisplay_2_p12));
  DipSwitch u_hex (.out(hex));
  Seven_Seg_Hex seven_seg_hex_10 (.d(hexdisplay_2_p14), .dp(hexdisplay_2_p15));
  vga_frontpanel vga_frontpanel_1 (.clock(DC), .PC(PC), .R0(R0), .R1(R1), .R2(R2), .R3(R3), .en(dipswitch_1_out));
  SixteenSeg sixteenseg_9 (.led(regdisplay_2_p1), .dp(regdisplay_2_p3));
  SixteenSeg sixteenseg_10 (.led(regdisplay_2_p5), .dp(regdisplay_2_p7));
  // regdisplay regdisplay_2: pin names not known; wires that end beside it: regdisplay_2_p1, rs_valid, regdisplay_2_p3, 1'b0, regdisplay_2_p5, rs, regdisplay_2_p7
  DipSwitch dipswitch_1 (.out(dipswitch_1_out));

  // Notes on the sheet:
  //   clock: Hz: 5
  //   DC: Hz: 2147483647
  //   rj45 Creates
endmodule
